// Logisim project 2bit 상하향 카운터.circ as structural Verilog: 1 circuit, main circuit main
module main (
  input  in_1,
  input  in_2,
  output out_3,
  output out_4,
  output [1:0] out_5,
  output out_6,
  output out_7
);

  wire and_1_out, and_2_out, and_3_out, and_4_out, clock_1_out, not_1_out, or_1_out;

  not not_1 (not_1_out, in_1);
  and and_1 (and_1_out, out_4, out_7, not_1_out);
  and and_2 (and_2_out, in_1, out_4, out_5[0]);
  and and_3 (and_3_out, out_5[0], not_1_out, out_3);
  and and_4 (and_4_out, out_7, out_3, in_1);
  or or_1 (or_1_out, and_1_out, and_2_out, and_3_out, and_4_out);
  Clock clock_1 (.out(clock_1_out));
  D_Flip_Flop d_ff_1 (.clk(clock_1_out), .D(or_1_out), .Q(out_3), .Qn(out_4));  // open: preset, en, reset
  D_Flip_Flop d_ff_2 (.clk(clock_1_out), .D(out_7), .Q(out_5[0]), .Qn(out_7));  // open: preset, en, reset

  assign out_5[1] = out_3;
  assign out_6 = out_5[0];
endmodule
