// Logisim project My.circ as structural Verilog
module Clock_Main (
);

  wire button_1_out, button_2_out, button_3_out, clock_body_1_alarm, clock_body_1_am, clock_body_1_out_11,
       clock_body_1_out_12, clock_body_1_out_13, clock_body_1_out_15, clock_body_1_out_16,
       clock_body_1_out_17, clock_body_1_pm;
  wire [3:0] clock_body_1_out_4, clock_body_1_out_5, clock_body_1_out_6, clock_body_1_out_7,
       clock_body_1_out_8, clock_body_1_out_9;

  Button button_1 (.out(button_1_out));
  LED led_1 (.in(clock_body_1_alarm));
  LED led_2 (.in(clock_body_1_am));
  LED led_3 (.in(clock_body_1_pm));
  Hex_Digit_Display hex_digit_display_1 (.value(clock_body_1_out_4));  // open: dp
  LED led_4 (.in(clock_body_1_out_15));
  Hex_Digit_Display hex_digit_display_2 (.value(clock_body_1_out_5));  // open: dp
  LED led_5 (.in(clock_body_1_out_16));
  Hex_Digit_Display hex_digit_display_3 (.value(clock_body_1_out_6));  // open: dp
  Hex_Digit_Display hex_digit_display_4 (.value(clock_body_1_out_7));  // open: dp
  Clock_Body clock_body_1 (
    .out_11(clock_body_1_out_11), .out_12(clock_body_1_out_12), .out_13(clock_body_1_out_13),
    .out_15(clock_body_1_out_15), .out_16(clock_body_1_out_16), .out_17(clock_body_1_out_17),
    .Mode(button_1_out), .Alarm(clock_body_1_alarm), .out_4(clock_body_1_out_4), .out_5(clock_body_1_out_5),
    .out_6(clock_body_1_out_6), .out_7(clock_body_1_out_7), .out_8(clock_body_1_out_8),
    .out_9(clock_body_1_out_9), .in_3(button_3_out), .in_1(button_2_out), .AM(clock_body_1_am),
    .PM(clock_body_1_pm));
  LED led_6 (.in(clock_body_1_out_17));
  Hex_Digit_Display hex_digit_display_5 (.value(clock_body_1_out_8));  // open: dp
  LED led_7 (.in(clock_body_1_out_11));
  LED led_8 (.in(clock_body_1_out_12));
  Hex_Digit_Display hex_digit_display_6 (.value(clock_body_1_out_9));  // open: dp
  LED led_9 (.in(clock_body_1_out_13));
  Button button_2 (.out(button_2_out));
  Button button_3 (.out(button_3_out));

  // Notes on the sheet:
  //   Mode
  //   Alarm Activation
  //   AM
  //   PM
  //   Time
  //   Alarm
  //   Timer
  //   Modify
  //   Stop
  //   Select
  //   Start & Reset
endmodule

// Clock
module Clock_Body (
  input  in_1,
  input  Mode,
  input  in_3,
  output [3:0] out_4,
  output [3:0] out_5,
  output [3:0] out_6,
  output [3:0] out_7,
  output [3:0] out_8,
  output [3:0] out_9,
  output AM,
  output out_11,
  output out_12,
  output out_13,
  output PM,
  output out_15,
  output out_16,
  output out_17,
  output Alarm
);

  wire alarm_1_out_6, alarm_1_out_7, alarm_1_out_8, and_1_out, and_2_out, and_3_out, and_4_out, and_5_out,
       and_6_out, and_7_out, and_8_out, and_9_out, bitselector_1_out, bitselector_7_out, clock_1_out,
       digital_clock_1_out_4, digital_clock_1_out_5, h1, h2, h3, h4, h5, M1, M2, M3, M4, M5, M6, M7,
       not_1_out, not_2_out, not_3_out, t_ff_2_q, t_ff_3_q, xnor_1_out, xnor_2_out, xnor_3_out, xnor_4_out,
       xnor_5_out, xnor_6_out, xnor_7_out, xnor_8_out, xnor_9_out, xnor_10_out, xnor_11_out, xnor_12_out;
  wire [1:0] n3_counter_1_out_4;
  wire [2:0] alarm_1_out_20, alarm_1_out_28, bitselector_3_out, bitselector_5_out, bitselector_9_out,
       bitselector_11_out, bitselector_13_out, bitselector_15_out, digital_clock_1_out_19, or_9_out,
       timer_1_out_16, timer_1_out_24;
  wire [3:0] alarm_1_out_12, alarm_1_out_16, alarm_1_out_24, bitselector_2_out, bitselector_4_out,
       bitselector_6_out, bitselector_8_out, bitselector_10_out, bitselector_12_out, bitselector_14_out,
       bitselector_16_out, bitselector_17_out, bitselector_18_out, digital_clock_1_out_23, timer_1_out_8,
       timer_1_out_12, timer_1_out_20, timer_1_out_28;

  or or_1 (out_4[2], 1'b0, bitselector_13_out[2]);
  Hex_Digit_Display hex_digit_display_1 (.value({1'b0, out_4[2:0]}));  // open: dp
  or or_2 (out_4[0], bitselector_13_out[0], bitselector_1_out, bitselector_7_out);
  or or_3 (out_4[1], 1'b0, bitselector_13_out[1]);
  xnor xnor_1 (xnor_1_out, alarm_1_out_8, h1);
  xnor xnor_2 (xnor_2_out, alarm_1_out_12[0], h2);
  Hex_Digit_Display hex_digit_display_2 (.value(out_5));  // open: dp
  assign out_5 = bitselector_14_out | bitselector_2_out | bitselector_8_out;  // OR_Gate or_4, 4 bits wide
  xnor xnor_3 (xnor_3_out, alarm_1_out_12[1], h3);
  xnor xnor_4 (xnor_4_out, alarm_1_out_12[2], h4);
  xnor xnor_5 (xnor_5_out, alarm_1_out_12[3], h5);
  and and_1 (and_1_out, xnor_1_out, xnor_2_out, xnor_3_out, xnor_4_out, xnor_5_out, xnor_6_out, xnor_8_out, xnor_9_out, xnor_10_out, xnor_11_out, xnor_12_out, xnor_7_out);
  Hex_Digit_Display hex_digit_display_3 (.value({1'b0, out_6[2:0]}));  // open: dp
  assign out_6[2:0] = bitselector_15_out | bitselector_3_out | bitselector_9_out;  // OR_Gate or_5, 3 bits wide
  xnor xnor_6 (xnor_6_out, alarm_1_out_28[0], M1);
  xnor xnor_7 (xnor_7_out, alarm_1_out_28[1], M2);
  Hex_Digit_Display hex_digit_display_4 (.value(out_7));  // open: dp
  assign out_7 = bitselector_16_out | bitselector_4_out | bitselector_10_out;  // OR_Gate or_6, 4 bits wide
  xnor xnor_8 (xnor_8_out, alarm_1_out_28[2], M3);
  T_Flip_Flop t_ff_1 (.clk(clock_1_out), .T(and_1_out), .Q(Alarm));  // open: Qn, preset, reset, en
  or or_7 (out_8[3], bitselector_17_out[3], 1'b0);
  or or_8 (out_8[2], bitselector_17_out[2], or_9_out[2]);
  xnor xnor_9 (xnor_9_out, alarm_1_out_16[0], M4);
  xnor xnor_10 (xnor_10_out, alarm_1_out_16[1], M5);
  Hex_Digit_Display hex_digit_display_5 (.value(out_8));  // open: dp
  assign or_9_out = bitselector_5_out | bitselector_11_out;  // OR_Gate or_9, 3 bits wide
  xnor xnor_11 (xnor_11_out, alarm_1_out_16[2], M6);
  xnor xnor_12 (xnor_12_out, alarm_1_out_16[3], M7);
  Hex_Digit_Display hex_digit_display_6 (.value(out_9));  // open: dp
  assign out_9 = bitselector_18_out | bitselector_6_out | bitselector_12_out;  // OR_Gate or_10, 4 bits wide
  BitSelector #(.width(1)) bitselector_1 (.in(alarm_1_out_8), .out(bitselector_1_out), .sel(not_2_out));
  BitSelector #(.width(4), .group(4)) bitselector_2 (.in(alarm_1_out_12), .out(bitselector_2_out), .sel(not_2_out));
  BitSelector #(.width(3), .group(3)) bitselector_3 (.in(alarm_1_out_28), .out(bitselector_3_out), .sel(not_2_out));
  BitSelector #(.width(4), .group(4)) bitselector_4 (.in(alarm_1_out_16), .out(bitselector_4_out), .sel(not_2_out));
  BitSelector #(.width(3), .group(3)) bitselector_5 (.in(alarm_1_out_20), .out(bitselector_5_out), .sel(not_2_out));
  BitSelector #(.width(4), .group(4)) bitselector_6 (.in(alarm_1_out_24), .out(bitselector_6_out), .sel(not_2_out));
  or or_11 (out_8[1], bitselector_17_out[1], or_9_out[1]);
  or or_12 (out_8[0], bitselector_17_out[0], or_9_out[0]);
  LED led_1 (.in(out_11));
  LED led_2 (.in(out_12));
  LED led_3 (.in(out_13));
  BitSelector #(.width(1)) bitselector_7 (.in(h1), .out(bitselector_7_out), .sel(not_1_out));
  BitSelector #(.width(4), .group(4)) bitselector_8 (.in({h5, h4, h3, h2}), .out(bitselector_8_out), .sel(not_1_out));
  BitSelector #(.width(3), .group(3)) bitselector_9 (.in({M3, M2, M1}), .out(bitselector_9_out), .sel(not_1_out));
  BitSelector #(.width(4), .group(4)) bitselector_10 (.in({M7, M6, M5, M4}), .out(bitselector_10_out), .sel(not_1_out));
  BitSelector #(.width(3), .group(3)) bitselector_11 (
    .in(digital_clock_1_out_19), .out(bitselector_11_out), .sel(not_1_out));
  BitSelector #(.width(4), .group(4)) bitselector_12 (
    .in(digital_clock_1_out_23), .out(bitselector_12_out), .sel(not_1_out));
  BitSelector #(.width(3), .group(3)) bitselector_13 (.in(timer_1_out_16), .out(bitselector_13_out), .sel(not_3_out));
  BitSelector #(.width(4), .group(4)) bitselector_14 (.in(timer_1_out_20), .out(bitselector_14_out), .sel(not_3_out));
  BitSelector #(.width(3), .group(3)) bitselector_15 (.in(timer_1_out_24), .out(bitselector_15_out), .sel(not_3_out));
  BitSelector #(.width(4), .group(4)) bitselector_16 (.in(timer_1_out_28), .out(bitselector_16_out), .sel(not_3_out));
  BitSelector #(.width(4), .group(4)) bitselector_17 (.in(timer_1_out_8), .out(bitselector_17_out), .sel(not_3_out));
  BitSelector #(.width(4), .group(4)) bitselector_18 (.in(timer_1_out_12), .out(bitselector_18_out), .sel(not_3_out));
  Digital_Clock digital_clock_1 (
    .out_7(h1), .out_8(h5), .out_9(h4), .out_10(h3), .out_11(h2), .out_25(M3), .out_26(M2), .out_27(M1),
    .out_12(M7), .out_13(M6), .out_14(M5), .out_15(M4), .out_17(digital_clock_1_out_19[2]),
    .out_18(digital_clock_1_out_19[1]), .out_19(digital_clock_1_out_19[0]),
    .out_20(digital_clock_1_out_23[3]), .out_21(digital_clock_1_out_23[2]),
    .out_22(digital_clock_1_out_23[1]), .out_23(digital_clock_1_out_23[0]), .in_3(clock_1_out),
    .out_4(digital_clock_1_out_4), .out_5(digital_clock_1_out_5));  // open: in_1, out_24, out_16, out_6, in_2
  Alarm alarm_1 (
    .in_2(and_4_out), .in_1(and_2_out), .out_8(alarm_1_out_8), .out_9(alarm_1_out_12[3]),
    .out_10(alarm_1_out_12[2]), .out_11(alarm_1_out_12[1]), .out_12(alarm_1_out_12[0]),
    .out_26(alarm_1_out_28[2]), .out_27(alarm_1_out_28[1]), .out_28(alarm_1_out_28[0]),
    .out_13(alarm_1_out_16[3]), .out_14(alarm_1_out_16[2]), .out_15(alarm_1_out_16[1]),
    .out_16(alarm_1_out_16[0]), .out_18(alarm_1_out_20[2]), .out_19(alarm_1_out_20[1]),
    .out_20(alarm_1_out_20[0]), .out_21(alarm_1_out_24[3]), .out_22(alarm_1_out_24[2]),
    .out_23(alarm_1_out_24[1]), .out_24(alarm_1_out_24[0]), .out_4(out_15), .out_5(out_16), .out_3(out_17),
    .out_6(alarm_1_out_6), .out_7(alarm_1_out_7));  // open: out_25, out_17
  TImer timer_1 (
    .in_1(and_3_out), .in_3(and_5_out), .out_14(timer_1_out_16[2]), .out_15(timer_1_out_16[1]),
    .out_16(timer_1_out_16[0]), .out_22(timer_1_out_24[2]), .out_23(timer_1_out_24[1]),
    .out_24(timer_1_out_24[0]), .out_25(timer_1_out_28[3]), .out_26(timer_1_out_28[2]),
    .out_27(timer_1_out_28[1]), .out_28(timer_1_out_28[0]), .out_5(timer_1_out_8[3]),
    .out_6(timer_1_out_8[2]), .out_7(timer_1_out_8[1]), .out_8(timer_1_out_8[0]), .out_9(timer_1_out_12[3]),
    .out_10(timer_1_out_12[2]), .out_11(timer_1_out_12[1]), .out_12(timer_1_out_12[0]),
    .out_17(timer_1_out_20[3]), .out_18(timer_1_out_20[2]), .out_19(timer_1_out_20[1]),
    .out_20(timer_1_out_20[0]), .in_4(clock_1_out));  // open: in_2, out_13, out_21
  Clock clock_1 (.out(clock_1_out));
  not not_1 (not_1_out, out_11);
  not not_2 (not_2_out, out_12);
  not not_3 (not_3_out, out_13);
  _3_Counter u_3_counter_1 (.in_1(Mode), .out_3(n3_counter_1_out_4[1]), .out_4(n3_counter_1_out_4[0]));  // open: in_2
  and and_2 (and_2_out, in_1, out_12);
  and and_3 (and_3_out, t_ff_3_q, out_13);
  Demultiplexer #(.select(3)) demultiplexer_1 (
    .out1(out_11), .out2(out_12), .out3(out_13), .in(1'b1), .sel({1'b0, n3_counter_1_out_4}), .en(1'b1));  // open: out0, out4, out5, out6, out7
  and and_4 (and_4_out, in_3, out_12);
  and and_5 (and_5_out, t_ff_2_q, out_13);
  T_Flip_Flop t_ff_2 (.clk(in_3), .T(1'b1), .Q(t_ff_2_q));  // open: Qn, preset, reset, en
  T_Flip_Flop t_ff_3 (.clk(in_1), .T(1'b1), .Q(t_ff_3_q));  // open: Qn, preset, reset, en
  and and_6 (and_6_out, out_11, digital_clock_1_out_4);
  and and_7 (and_7_out, out_11, digital_clock_1_out_5);
  and and_8 (and_8_out, out_12, alarm_1_out_6);
  and and_9 (and_9_out, out_12, alarm_1_out_7);
  or or_13 (AM, and_6_out, and_8_out);
  or or_14 (PM, and_7_out, and_9_out);

  assign out_4[3] = 1'b0;
  assign out_6[3] = 1'b0;

  // Notes on the sheet:
  //   Time
  //   Alarm
  //   Timer
endmodule

module Digital_Clock (
  input  in_1,
  input  in_2,
  input  in_3,
  output out_4,
  output out_5,
  output out_6,
  output out_7,
  output out_8,
  output out_9,
  output out_10,
  output out_11,
  output out_12,
  output out_13,
  output out_14,
  output out_15,
  output out_16,
  output out_17,
  output out_18,
  output out_19,
  output out_20,
  output out_21,
  output out_22,
  output out_23,
  output out_24,
  output out_25,
  output out_26,
  output out_27
);

  wire sync_6_counter_1_out_7, sync_6_counter_2_out_7, sync_10_counter_1_out_8, sync_10_counter_2_out_8,
       sync_12_counter_1_out_4, sync_12_counter_1_out_5, sync_12_counter_1_out_6, sync_12_counter_1_out_7,
       sync_12_counter_1_out_8;

  Hex_Digit_Display hex_digit_display_1 (.value({{3{in_1}}, out_7}));  // open: dp
  LED led_1 (.in(out_4));
  LED led_2 (.in(out_5));
  _12_Decoder u_12_decoder_1 (
    .in_1(sync_12_counter_1_out_7), .in_2(sync_12_counter_1_out_5), .in_3(sync_12_counter_1_out_4),
    .in_4(sync_12_counter_1_out_6), .out_5(out_7), .out_6(out_8), .out_7(out_9), .out_8(out_10),
    .out_9(out_11));
  AM_PM am_pm_1 (.in_1(in_3), .in_2(sync_12_counter_1_out_8), .out_3(out_5), .out_4(out_4));
  Hex_Digit_Display hex_digit_display_2 (.value({out_8, out_9, out_10, out_11}));  // open: dp
  Sync_12_Counter sync_12_counter_1 (
    .in_1(sync_6_counter_1_out_7), .in_2(in_3), .out_8(sync_12_counter_1_out_8),
    .out_6(sync_12_counter_1_out_6), .out_4(sync_12_counter_1_out_4), .out_5(sync_12_counter_1_out_5),
    .out_7(sync_12_counter_1_out_7), .in_3(in_2));
  Hex_Digit_Display hex_digit_display_3 (.value({in_1, out_25, out_26, out_27}));  // open: dp
  Sync_6_Counter sync_6_counter_1 (
    .in_1(in_3), .out_4(out_27), .out_5(out_26), .out_6(out_25), .in_2(sync_10_counter_1_out_8),
    .out_7(sync_6_counter_1_out_7), .in_3(in_2));
  Hex_Digit_Display hex_digit_display_4 (.value({out_12, out_13, out_14, out_15}));  // open: dp
  Sync_10_Counter sync_10_counter_1 (
    .out_7(out_12), .out_4(out_15), .out_5(out_14), .out_6(out_13), .in_1(in_3),
    .in_2(sync_6_counter_2_out_7), .out_8(sync_10_counter_1_out_8), .in_3(in_2));
  Hex_Digit_Display hex_digit_display_5 (.value({in_1, out_17, out_18, out_19}));  // open: dp
  Sync_6_Counter sync_6_counter_2 (
    .in_1(in_3), .out_4(out_19), .out_5(out_18), .out_6(out_17), .in_2(sync_10_counter_2_out_8),
    .out_7(sync_6_counter_2_out_7), .in_3(in_2));
  Hex_Digit_Display hex_digit_display_6 (.value({out_20, out_21, out_22, out_23}));  // open: dp
  Sync_10_Counter sync_10_counter_2 (
    .out_7(out_20), .out_4(out_23), .out_5(out_22), .out_6(out_21), .in_1(in_3), .in_2(1'b1),
    .out_8(sync_10_counter_2_out_8), .in_3(in_2));

  assign out_6 = in_3;
  assign out_16 = in_1;
  assign out_24 = in_1;
endmodule

module TImer (
  input  in_1,
  input  in_2,
  input  in_3,
  input  in_4,
  output out_5,
  output out_6,
  output out_7,
  output out_8,
  output out_9,
  output out_10,
  output out_11,
  output out_12,
  output out_13,
  output out_14,
  output out_15,
  output out_16,
  output out_17,
  output out_18,
  output out_19,
  output out_20,
  output out_21,
  output out_22,
  output out_23,
  output out_24,
  output out_25,
  output out_26,
  output out_27,
  output out_28
);

  wire and_1_out, not_1_out, not_2_out, not_3_out, sync_6_counter_1_out_4, sync_6_counter_1_out_5,
       sync_6_counter_1_out_6, sync_6_counter_2_out_4, sync_6_counter_2_out_5, sync_6_counter_2_out_6,
       sync_6_counter_2_out_7, sync_10_counter_1_out_4, sync_10_counter_1_out_5, sync_10_counter_1_out_6,
       sync_10_counter_1_out_7, sync_10_counter_1_out_8, sync_10_counter_2_out_4, sync_10_counter_2_out_5,
       sync_10_counter_2_out_6, sync_10_counter_2_out_7, sync_10_counter_2_out_8, sync_10_counter_3_out_4,
       sync_10_counter_3_out_5, sync_10_counter_3_out_6, sync_10_counter_3_out_7, sync_10_counter_3_out_8,
       sync_10_counter_4_out_4, sync_10_counter_4_out_5, sync_10_counter_4_out_6, sync_10_counter_4_out_7,
       sync_10_counter_4_out_8;

  and and_1 (and_1_out, in_1, in_3);
  not not_1 (not_1_out, and_1_out);
  LED led_1 (.in(in_3));
  LED led_2 (.in(not_1_out));
  not not_2 (not_2_out, in_3);
  not not_3 (not_3_out, in_3);
  Sync_6_Counter sync_6_counter_1 (
    .in_1(in_4), .out_4(sync_6_counter_1_out_4), .out_5(sync_6_counter_1_out_5),
    .out_6(sync_6_counter_1_out_6), .in_2(sync_10_counter_1_out_8), .in_3(not_3_out));  // open: out_7
  Hex_Digit_Display hex_digit_display_1 (.value({out_13, out_14, out_15, out_16}));  // open: dp
  _4bits_Register u_4bits_register_1 (
    .in_2(sync_6_counter_1_out_4), .in_3(sync_6_counter_1_out_5), .in_4(sync_6_counter_1_out_6), .in_5(in_2),
    .in_7(not_1_out), .in_8(not_1_out), .out_9(out_16), .out_10(out_15), .out_11(out_14), .out_12(out_13),
    .in_6(in_4), .in_1(not_2_out));
  Sync_10_Counter sync_10_counter_1 (
    .out_7(sync_10_counter_1_out_7), .out_4(sync_10_counter_1_out_4), .out_5(sync_10_counter_1_out_5),
    .out_6(sync_10_counter_1_out_6), .in_1(in_4), .in_2(sync_6_counter_2_out_7),
    .out_8(sync_10_counter_1_out_8), .in_3(not_3_out));
  Hex_Digit_Display hex_digit_display_2 (.value({out_17, out_18, out_19, out_20}));  // open: dp
  _4bits_Register u_4bits_register_2 (
    .in_2(sync_10_counter_1_out_4), .in_3(sync_10_counter_1_out_5), .in_4(sync_10_counter_1_out_6),
    .in_5(sync_10_counter_1_out_7), .in_7(not_1_out), .in_8(not_1_out), .out_9(out_20), .out_10(out_19),
    .out_11(out_18), .out_12(out_17), .in_6(in_4), .in_1(not_2_out));
  Hex_Digit_Display hex_digit_display_3 (.value({out_21, out_22, out_23, out_24}));  // open: dp
  _4bits_Register u_4bits_register_3 (
    .in_2(sync_6_counter_2_out_4), .in_3(sync_6_counter_2_out_5), .in_4(sync_6_counter_2_out_6), .in_5(in_2),
    .in_7(not_1_out), .in_8(not_1_out), .out_9(out_24), .out_10(out_23), .out_11(out_22), .out_12(out_21),
    .in_6(in_4), .in_1(not_2_out));
  Sync_6_Counter sync_6_counter_2 (
    .in_1(in_4), .out_4(sync_6_counter_2_out_4), .out_5(sync_6_counter_2_out_5),
    .out_6(sync_6_counter_2_out_6), .in_2(sync_10_counter_2_out_8), .out_7(sync_6_counter_2_out_7),
    .in_3(not_3_out));
  Hex_Digit_Display hex_digit_display_4 (.value({out_25, out_26, out_27, out_28}));  // open: dp
  _4bits_Register u_4bits_register_4 (
    .in_2(sync_10_counter_2_out_4), .in_3(sync_10_counter_2_out_5), .in_4(sync_10_counter_2_out_6),
    .in_5(sync_10_counter_2_out_7), .in_7(not_1_out), .in_8(not_1_out), .out_9(out_28), .out_10(out_27),
    .out_11(out_26), .out_12(out_25), .in_6(in_4), .in_1(not_2_out));
  Sync_10_Counter sync_10_counter_2 (
    .out_7(sync_10_counter_2_out_7), .out_4(sync_10_counter_2_out_4), .out_5(sync_10_counter_2_out_5),
    .out_6(sync_10_counter_2_out_6), .in_1(in_4), .in_2(sync_10_counter_3_out_8),
    .out_8(sync_10_counter_2_out_8), .in_3(not_3_out));
  Sync_10_Counter sync_10_counter_3 (
    .out_7(sync_10_counter_3_out_7), .out_4(sync_10_counter_3_out_4), .out_5(sync_10_counter_3_out_5),
    .out_6(sync_10_counter_3_out_6), .in_1(in_4), .in_2(sync_10_counter_4_out_8),
    .out_8(sync_10_counter_3_out_8), .in_3(not_3_out));
  Hex_Digit_Display hex_digit_display_5 (.value({out_5, out_6, out_7, out_8}));  // open: dp
  _4bits_Register u_4bits_register_5 (
    .in_2(sync_10_counter_3_out_4), .in_3(sync_10_counter_3_out_5), .in_4(sync_10_counter_3_out_6),
    .in_5(sync_10_counter_3_out_7), .in_7(not_1_out), .in_8(not_1_out), .out_9(out_8), .out_10(out_7),
    .out_11(out_6), .out_12(out_5), .in_6(in_4), .in_1(not_2_out));
  Sync_10_Counter sync_10_counter_4 (
    .out_7(sync_10_counter_4_out_7), .out_4(sync_10_counter_4_out_4), .out_5(sync_10_counter_4_out_5),
    .out_6(sync_10_counter_4_out_6), .in_1(in_4), .in_2(1'b1), .out_8(sync_10_counter_4_out_8),
    .in_3(not_3_out));
  Hex_Digit_Display hex_digit_display_6 (.value({out_9, out_10, out_11, out_12}));  // open: dp
  _4bits_Register u_4bits_register_6 (
    .in_2(sync_10_counter_4_out_4), .in_3(sync_10_counter_4_out_5), .in_4(sync_10_counter_4_out_6),
    .in_5(sync_10_counter_4_out_7), .in_7(not_1_out), .in_8(not_1_out), .out_9(out_12), .out_10(out_11),
    .out_11(out_10), .out_12(out_9), .in_6(in_4), .in_1(not_2_out));
endmodule

module Alarm (
  input  in_1,
  input  in_2,
  output out_3,
  output out_4,
  output out_5,
  output out_6,
  output out_7,
  output out_8,
  output out_9,
  output out_10,
  output out_11,
  output out_12,
  output out_13,
  output out_14,
  output out_15,
  output out_16,
  output out_17,
  output out_18,
  output out_19,
  output out_20,
  output out_21,
  output out_22,
  output out_23,
  output out_24,
  output out_25,
  output out_26,
  output out_27,
  output out_28
);

  wire not_1_out, sync_10_counter_1_out_8, sync_10_counter_2_out_8, sync_12_counter_1_out_4,
       sync_12_counter_1_out_5, sync_12_counter_1_out_6, sync_12_counter_1_out_7, sync_12_counter_1_out_8;
  wire [1:0] n3_counter_1_out_4;

  LED led_1 (.in(out_4));
  Hex_Digit_Display hex_digit_display_1 (.value({3'b000, out_8}));  // open: dp
  LED led_2 (.in(out_6));
  LED led_3 (.in(out_7));
  _12_Decoder u_12_decoder_1 (
    .in_1(sync_12_counter_1_out_7), .in_2(sync_12_counter_1_out_5), .in_3(sync_12_counter_1_out_4),
    .in_4(sync_12_counter_1_out_6), .out_5(out_8), .out_6(out_9), .out_7(out_10), .out_8(out_11),
    .out_9(out_12));
  AM_PM am_pm_1 (.in_1(out_4), .in_2(sync_12_counter_1_out_8), .out_3(out_7), .out_4(out_6));
  Hex_Digit_Display hex_digit_display_2 (.value({out_9, out_10, out_11, out_12}));  // open: dp
  Sync_12_Counter sync_12_counter_1 (
    .in_1(1'b1), .in_2(out_4), .out_8(sync_12_counter_1_out_8), .out_6(sync_12_counter_1_out_6),
    .out_4(sync_12_counter_1_out_4), .out_5(sync_12_counter_1_out_5), .out_7(sync_12_counter_1_out_7),
    .in_3(1'b0));
  LED led_4 (.in(out_5));
  Hex_Digit_Display hex_digit_display_3 (.value({1'b0, out_26, out_27, out_28}));  // open: dp
  Sync_6_Counter sync_6_counter_1 (
    .in_1(out_5), .out_4(out_28), .out_5(out_27), .out_6(out_26), .in_2(sync_10_counter_1_out_8), .in_3(1'b0));  // open: out_7
  Hex_Digit_Display hex_digit_display_4 (.value({out_13, out_14, out_15, out_16}));  // open: dp
  Sync_10_Counter sync_10_counter_1 (
    .out_7(out_13), .out_4(out_16), .out_5(out_15), .out_6(out_14), .in_1(out_5), .in_2(1'b1),
    .out_8(sync_10_counter_1_out_8), .in_3(1'b0));
  LED led_5 (.in(out_3));
  Hex_Digit_Display hex_digit_display_5 (.value({1'b0, out_18, out_19, out_20}));  // open: dp
  Sync_6_Counter sync_6_counter_2 (
    .in_1(out_3), .out_4(out_20), .out_5(out_19), .out_6(out_18), .in_2(sync_10_counter_2_out_8), .in_3(1'b0));  // open: out_7
  Hex_Digit_Display hex_digit_display_6 (.value({out_21, out_22, out_23, out_24}));  // open: dp
  not not_1 (not_1_out, in_2);
  Sync_10_Counter sync_10_counter_2 (
    .out_7(out_21), .out_4(out_24), .out_5(out_23), .out_6(out_22), .in_1(out_3), .in_2(1'b1),
    .out_8(sync_10_counter_2_out_8), .in_3(1'b0));
  _3_Counter u_3_counter_1 (
    .in_1(not_1_out), .out_3(n3_counter_1_out_4[1]), .out_4(n3_counter_1_out_4[0]));  // open: in_2
  Demultiplexer #(.select(3)) demultiplexer_1 (
    .out1(out_3), .out2(out_5), .out3(out_4), .in(in_1), .sel({1'b0, n3_counter_1_out_4}), .en(1'b1));  // open: out0, out4, out5, out6, out7

  assign out_17 = 1'b0;
  assign out_25 = 1'b0;
endmodule

module Sync_6_Counter (
  input  in_1,
  input  in_2,
  input  in_3,
  output out_4,
  output out_5,
  output out_6,
  output out_7
);

  wire and_1_out, and_2_out, and_3_out, and_4_out, and_5_out, and_6_out, or_1_out;

  J_K_Flip_Flop j_k_ff_1 (.J(in_2), .clk(in_1), .K(in_2), .Q(out_4), .reset(or_1_out));  // open: Qn, preset, en
  and and_1 (and_1_out, out_4, out_4, in_2);
  J_K_Flip_Flop j_k_ff_2 (
    .J(and_1_out), .clk(in_1), .K(and_2_out), .Q(out_5), .reset(or_1_out));  // open: Qn, preset, en
  and and_2 (and_2_out, out_4, in_2);
  and and_3 (and_3_out, out_4, out_5);
  and and_4 (and_4_out, out_5, out_6);
  or or_1 (or_1_out, and_4_out, in_3);
  and and_5 (and_5_out, in_2, and_3_out);
  J_K_Flip_Flop j_k_ff_3 (
    .J(and_5_out), .clk(in_1), .K(and_6_out), .Q(out_6), .reset(or_1_out));  // open: Qn, preset, en
  and and_6 (and_6_out, and_3_out, in_2);
  and and_7 (out_7, in_2, out_4, out_6);
endmodule

module Sync_10_Counter (
  input  in_1,
  input  in_2,
  input  in_3,
  output out_4,
  output out_5,
  output out_6,
  output out_7,
  output out_8
);

  wire and_1_out, and_2_out, and_3_out, and_4_out, and_5_out, and_6_out, and_8_out, and_9_out, and_10_out,
       and_11_out, j_k_ff_4_qn, or_1_out;

  J_K_Flip_Flop j_k_ff_1 (.J(in_2), .clk(in_1), .K(in_2), .Q(out_4), .reset(in_3));  // open: Qn, preset, en
  and and_1 (and_1_out, out_4, j_k_ff_4_qn);
  and and_2 (and_2_out, and_1_out, in_2);
  and and_3 (and_3_out, and_1_out, in_2);
  J_K_Flip_Flop j_k_ff_2 (.J(and_2_out), .clk(in_1), .K(and_3_out), .Q(out_5), .reset(in_3));  // open: Qn, preset, en
  and and_4 (and_4_out, out_4, out_5);
  and and_5 (and_5_out, and_4_out, in_2);
  and and_6 (and_6_out, and_4_out, in_2);
  and and_7 (out_8, in_2, out_7, out_4);
  J_K_Flip_Flop j_k_ff_3 (.J(and_5_out), .clk(in_1), .K(and_6_out), .Q(out_6), .reset(in_3));  // open: Qn, preset, en
  and and_8 (and_8_out, out_7, out_4);
  or or_1 (or_1_out, and_8_out, and_9_out);
  and and_9 (and_9_out, and_4_out, out_6);
  and and_10 (and_10_out, or_1_out, in_2);
  J_K_Flip_Flop j_k_ff_4 (
    .J(and_10_out), .clk(in_1), .K(and_11_out), .Q(out_7), .Qn(j_k_ff_4_qn), .reset(in_3));  // open: preset, en
  and and_11 (and_11_out, or_1_out, in_2);
endmodule

module Sync_12_Counter (
  input  in_1,
  input  in_2,
  input  in_3,
  output out_4,
  output out_5,
  output out_6,
  output out_7,
  output out_8
);

  wire and_1_out, and_2_out, and_3_out, and_4_out, and_5_out, and_6_out, and_7_out, or_1_out;

  T_Flip_Flop t_ff_1 (.clk(in_2), .T(in_1), .Q(out_6), .reset(or_1_out));  // open: Qn, preset, en
  and and_1 (and_1_out, in_1, out_6);
  and and_2 (and_2_out, and_1_out, in_1);
  T_Flip_Flop t_ff_2 (.clk(in_2), .T(and_2_out), .Q(out_4), .reset(or_1_out));  // open: Qn, preset, en
  and and_3 (and_3_out, and_1_out, out_4);
  T_Flip_Flop t_ff_3 (.clk(in_2), .T(and_4_out), .Q(out_5), .reset(or_1_out));  // open: Qn, preset, en
  and and_4 (and_4_out, and_3_out, in_1);
  and and_5 (and_5_out, and_3_out, out_5);
  and and_6 (and_6_out, and_5_out, in_1);
  or or_1 (or_1_out, and_7_out, in_3);
  T_Flip_Flop t_ff_4 (.clk(in_2), .T(and_6_out), .Q(out_7), .reset(or_1_out));  // open: Qn, preset, en
  and and_7 (and_7_out, out_5, out_7);
  and and_8 (out_8, in_1, out_7, out_4, out_6);
endmodule

module _12_Decoder (
  input  in_1,
  input  in_2,
  input  in_3,
  input  in_4,
  output out_5,
  output out_6,
  output out_7,
  output out_8,
  output out_9
);

  wire and_1_out, and_2_out, and_4_out, and_5_out, not_1_out, not_2_out, not_3_out, not_4_out;

  not not_1 (not_1_out, in_1);
  not not_2 (not_2_out, in_2);
  not not_3 (not_3_out, in_3);
  not not_4 (not_4_out, in_4);
  and and_1 (and_1_out, in_1, in_3);
  and and_2 (and_2_out, not_1_out, not_2_out, not_3_out, not_4_out);
  and and_3 (out_6, not_3_out, in_1);
  and and_4 (and_4_out, not_1_out, not_2_out, not_4_out);
  and and_5 (and_5_out, in_3, not_1_out);
  or or_1 (out_5, and_1_out, and_2_out);
  or or_2 (out_8, and_4_out, and_5_out);

  assign out_7 = in_2;
  assign out_9 = in_4;
endmodule

module AM_PM (
  input  in_1,
  input  in_2,
  output out_3,
  output out_4
);

  T_Flip_Flop t_ff_1 (.clk(in_1), .T(in_2), .Q(out_3), .Qn(out_4));  // open: preset, reset, en
endmodule

module _4bits_Register (
  input  in_1,
  input  in_2,
  input  in_3,
  input  in_4,
  input  in_5,
  input  in_6,
  input  in_7,
  input  in_8,
  output out_9,
  output out_10,
  output out_11,
  output out_12
);

  wire multiplexer_1_out, multiplexer_2_out, multiplexer_3_out, multiplexer_4_out;

  Multiplexer multiplexer_1 (.in0(out_9), .in1(in_2), .out(multiplexer_1_out), .sel(in_7), .en(in_8));
  Multiplexer multiplexer_2 (.in0(out_10), .in1(in_3), .out(multiplexer_2_out), .sel(in_7), .en(in_8));
  Multiplexer multiplexer_3 (.in0(out_11), .in1(in_4), .out(multiplexer_3_out), .sel(in_7), .en(in_8));
  Multiplexer multiplexer_4 (.in0(out_12), .in1(in_5), .out(multiplexer_4_out), .sel(in_7), .en(in_8));
  Register #(.width(1)) register_1 (.D(multiplexer_1_out), .Q(out_9), .clk(in_6), .clr(in_1));  // open: en
  Register #(.width(1)) register_2 (.D(multiplexer_2_out), .Q(out_10), .clk(in_6), .clr(in_1));  // open: en
  Register #(.width(1)) register_3 (.D(multiplexer_3_out), .Q(out_11), .clk(in_6), .clr(in_1));  // open: en
  Register #(.width(1)) register_4 (.D(multiplexer_4_out), .Q(out_12), .clk(in_6), .clr(in_1));  // open: en
endmodule

module _10_Counter (
  input  in_1,
  input  in_2,
  output out_3,
  output out_4,
  output out_5,
  output out_6
);

  wire and_1_out, or_1_out, t_ff_2_q, t_ff_4_q;

  T_Flip_Flop t_ff_1 (.clk(in_1), .T(1'b1), .Qn(out_3), .reset(or_1_out));  // open: Q, preset, en
  T_Flip_Flop t_ff_2 (.clk(out_3), .T(1'b1), .Q(t_ff_2_q), .Qn(out_4), .reset(or_1_out));  // open: preset, en
  T_Flip_Flop t_ff_3 (.clk(out_4), .T(1'b1), .Qn(out_5), .reset(or_1_out));  // open: Q, preset, en
  or or_1 (or_1_out, and_1_out, in_2);
  and and_1 (and_1_out, t_ff_2_q, t_ff_4_q);
  T_Flip_Flop t_ff_4 (.clk(out_5), .T(1'b1), .Q(t_ff_4_q), .Qn(out_6), .reset(or_1_out));  // open: preset, en
endmodule

module _3_Counter (
  input  in_1,
  input  in_2,
  output out_3,
  output out_4
);

  wire and_1_out, or_1_out, t_ff_1_q, t_ff_2_q;

  T_Flip_Flop t_ff_1 (.clk(in_1), .T(1'b1), .Q(t_ff_1_q), .Qn(out_3), .reset(or_1_out));  // open: preset, en
  and and_1 (and_1_out, t_ff_1_q, t_ff_2_q);
  or or_1 (or_1_out, and_1_out, in_2);
  T_Flip_Flop t_ff_2 (.clk(out_3), .T(1'b1), .Q(t_ff_2_q), .Qn(out_4), .reset(or_1_out));  // open: preset, en
endmodule
